# Fritzing sketch Lasertower-Sketch (saved by Fritzing 0.8.5b)
breadboards: 1

parts:
  Arduino = Arduino Uno (Rev3)
  Laser = LED - 5mm [color="Red (633nm)" package="5 mm [THT]"]
  J1 = Basic Servo
  J2 = Basic Servo
  R1 = Resistor [tolerance=±5% resistance=220 package=THT]

nets:
  N1: Arduino.D9_PWM, J1.pulse
  N2: Arduino.D10_PWM/SS, J2.pulse
  N3: Arduino.D12/MISO, R1.Pin_1
  5V: Arduino.5V, J1.vcc, J2.vcc
  GND: Arduino.GND, Laser.cathode, J1.gnd, J2.gnd
  N4: Laser.anode, R1.Pin_0
